# Fritzing sketch loadcell_measurement (saved by Fritzing 0.9.3b)

parts:
  Parts1 = SparkFun RedBoard [part_number=DEV-12757]
  SparkFun_Load_Cell_Amplifier_-_HX1 = SparkFun Load Cell Amplifier - HX711 [part_number=SEN-13879]
  S2 = Momentary Switch [package=ksa_sealed_tac_switch]
  R1 = Resistor [tolerance=±5% resistance=10k package="2512 [SMD]"]

nets:
  N1: Parts1.A4/SDA, SparkFun_Load_Cell_Amplifier_-_HX1.DAT
  N2: Parts1.GND, S2.3
  N3: Parts1.A5/SCL, SparkFun_Load_Cell_Amplifier_-_HX1.SCK
  N4: Parts1.D7, R1.Pin_1
  5V: Parts1.5V, SparkFun_Load_Cell_Amplifier_-_HX1.VDD

notes:
  To Load Cell

custom parts:
  SparkFun RedBoard: At SparkFun we use many Arduinos and we’re always looking for the simplest, most stable one. Each board is a bit different and no one board has everything we want, so we decided to make our own version that combines all our favorite features. The RedBoard combines the simplicity of the UNO’s Optiboot bootloader (which is used in the Pro series), the stability of the FTDI (which we all missed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
  SparkFun Load Cell Amplifier - HX711: The SparkFun Load Cell Amplifier is a small breakout board for the HX711 IC that allows you to easily read load cells to measure weight. By connecting the amplifier to your microcontroller you will be able to read the changes in the resistance of the load cell, and with some calibration you’ll be able to get very accurate weight measurements. This can be handy for creating your own industrial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
